# Fritzing sketch EstacaoMetereologica (saved by Fritzing 0.9.3b)
breadboards: 1

parts:
  Componente1 = Arduino Uno (Rev3)
  R1 = Rotary Potentiometer (Large) [maximum_resistance=10kΩ package=THT]
  LCD1 = LCD screen
  RHT3 = Humidity and Temperature Sensor RHT03

nets:
  N1: Componente1.A5/SCL, RHT3.Data-signal
  N2: Componente1.D2, LCD1.RS
  N3: Componente1.D3_PWM, LCD1.E
  N4: Componente1.D4, LCD1.DB4
  N5: Componente1.D5_PWM, LCD1.DB5
  N6: Componente1.D6_PWM, LCD1.DB6
  N7: Componente1.D7, LCD1.DB7
  5V: Componente1.5V, R1.leg1, LCD1.VDD, LCD1.LED+, RHT3.Vcc
  GND: Componente1.GND, R1.leg2, LCD1.VSS, LCD1.R/W, LCD1.LED-, RHT3.GND_2
  N8: R1.wiper, LCD1.V0
